// Digital circuit CPU_8bit.dig as structural Verilog
module CPU_8bit (
  input  [7:0] InputPort_7_0,
  input  clk,
  output HazardDetected,
  output [7:0] OutputPort_7_0
);

  wire Control_alu_src, Control_branchtaken, Control_memread, Control_memwrite, Control_writeenable,
       Control_writeoutput, DE_Reg_outalu_src, EM_Reg_outmemread, EM_Reg_outmemwrite, Match1_eq, Match2_eq,
       MW_Reg_outwriteenable, or_1_out;
  wire [1:0] comparator_1_eq;
  wire [2:0] Control_readreg1_2_0, Control_readreg2_2_0, Control_writereg_2_0, DE_Reg_outdestreg_2_0,
       EM_Reg_outdestreg_2_0, EM_Reg_outflags_2_0, MW_Reg_outdestreg_2_0, MW_Reg_outflags_2_0, not_1_out;
  wire [3:0] FD_Reg_outinstr_15_0, PC_pc_3_0;
  wire [7:0] ALU_p1, ALU_p2, ALU_p3, ALU_p7, Control_alu_op_7_0, Control_opcode_7_0, DE_Reg_outimmediate_7_0,
       DE_Reg_outregdata2_7_0, EM_Reg_outalu_result_7_0, EM_Reg_outopcode, multiplexer_1_out,
       MW_Reg_outopcode, MW_Reg_outresult_7_0, RAM_dataout_7_0, RegFile_readdata1_7_0, RegFile_readdata2_7_0;
  wire [15:0] multiplexer_3_out, ROM_instruction_15_0;
  wire [15:4] FD_Reg_outinstr_15_0_2;

  Comparator #(.Bits(8)) comparator_1 (.a(MW_Reg_outopcode), .b(8'h2), .eq(comparator_1_eq[0]));  // open: gt, lt
  Comparator #(.Bits(8)) comparator_2 (.a(MW_Reg_outopcode), .b(8'h20), .eq(comparator_1_eq[1]));  // open: gt, lt
  // Probe pc clock probe on clk
  // Probe on clk
  programCounter8 PC (
    .Clock(clk), .LoadData_3_0(FD_Reg_outinstr_15_0), .Load(Control_branchtaken), .Clear(1'b0),
    .PC_3_0(PC_pc_3_0));
  controlUnit Control (
    .Instruction_15_0(multiplexer_3_out), .Flags_2_0(MW_Reg_outflags_2_0), .ALU_src(Control_alu_src),
    .OpCode_7_0(Control_opcode_7_0), .ReadReg2_2_0(Control_readreg2_2_0),
    .ReadReg1_2_0(Control_readreg1_2_0), .WriteEnable(Control_writeenable), .MemRead(Control_memread),
    .MemWrite(Control_memwrite), .ALU_OP_7_0(Control_alu_op_7_0), .WriteReg_2_0(Control_writereg_2_0),
    .BranchTaken(Control_branchtaken), .WriteOutput(Control_writeoutput));
  // alu8bit ALU: pin names not known; wires that end beside it: ALU_p1, ALU_p2, ALU_p3, clk, clk, not_1_out[1], ALU_p7, not_1_out[0]
  dataRAM RAM (
    .Address_7_0(EM_Reg_outalu_result_7_0), .DataIn_7_0(EM_Reg_outalu_result_7_0),
    .MemWrite(EM_Reg_outmemwrite), .MemRead(EM_Reg_outmemread), .Clock(clk), .DataOut_7_0(RAM_dataout_7_0));
  // Probe on PC_pc_3_0
  // Probe on Control_opcode_7_0
  not not_1 (not_1_out[2], not_1_out[1]);
  // Probe on clk
  Multiplexer #(.Selector_Bits(2), .Bits(8)) multiplexer_1 (
    .sel(comparator_1_eq), .in_0(EM_Reg_outalu_result_7_0), .in_1(RAM_dataout_7_0), .in_2(InputPort_7_0),
    .in_3({8{1'b0}}), .out(multiplexer_1_out));
  // Probe EM probe on clk
  // Probe on clk
  registerFile8 RegFile (
    .Din_7_0(MW_Reg_outresult_7_0), .WriteEnable(MW_Reg_outwriteenable),
    .WriteReg_2_0(MW_Reg_outdestreg_2_0), .Clock(clk), .ReadReg1_2_0(Control_readreg2_2_0),
    .ReadReg2_2_0(Control_readreg1_2_0), .ReadData1_7_0(RegFile_readdata1_7_0),
    .ReadData2_7_0(RegFile_readdata2_7_0));
  EM_Register EM_Reg (
    .ALU_Result_7_0(ALU_p7), .DestReg_2_0(DE_Reg_outdestreg_2_0), .Flags_2_0(not_1_out),
    .MemWrite(Control_memwrite), .MemRead(Control_memread), .Clock(clk), .OpCode(ALU_p3),
    .OutALU_Result_7_0(EM_Reg_outalu_result_7_0), .OutDestReg_2_0(EM_Reg_outdestreg_2_0),
    .OutFlags_2_0(EM_Reg_outflags_2_0), .OutMemWrite(EM_Reg_outmemwrite), .OutMemRead(EM_Reg_outmemread),
    .OutOpCode(EM_Reg_outopcode));
  MW_Register MW_Reg (
    .Clock(clk), .FinalResult_7_0(multiplexer_1_out), .DestReg_2_0(EM_Reg_outdestreg_2_0),
    .WriteEnable(Control_writeenable), .Flags_2_0(EM_Reg_outflags_2_0), .OpCode(EM_Reg_outopcode),
    .OutResult_7_0(MW_Reg_outresult_7_0), .OutDestReg_2_0(MW_Reg_outdestreg_2_0),
    .OutWriteEnable(MW_Reg_outwriteenable), .OutFlags_2_0(MW_Reg_outflags_2_0), .OutOpCode(MW_Reg_outopcode));
  programROM ROM (.Address_3_0(PC_pc_3_0), .Instruction_15_0(ROM_instruction_15_0));
  // Probe on RegFile_readdata1_7_0
  Register #(.Bits(8)) OutputBuffer (.D(MW_Reg_outresult_7_0), .C(clk), .en(Control_writeoutput), .Q(OutputPort_7_0));
  // Probe on Control_writeoutput
  // Probe fd clock on clk
  // Probe on clk
  FD_Register FD_Reg (
    .Instruction_15_0(ROM_instruction_15_0), .PC_3_0(PC_pc_3_0), .Clock(clk),
    .OutInstr_15_0({FD_Reg_outinstr_15_0_2, FD_Reg_outinstr_15_0}));  // open: OutPC_3_0
  DE_Register DE_Reg (
    .RegData1_7_0(RegFile_readdata1_7_0), .RegData2_7_0(RegFile_readdata2_7_0),
    .Immediate_4_0({FD_Reg_outinstr_15_0_2[4], FD_Reg_outinstr_15_0}), .OpCode_7_0(Control_alu_op_7_0),
    .DestReg_2_0(Control_writereg_2_0), .Clock(clk), .ALU_src(Control_alu_src), .OutRegData1_7_0(ALU_p1),
    .OutRegData2_7_0(DE_Reg_outregdata2_7_0), .OutOpCode_7_0(ALU_p3),
    .OutImmediate_7_0(DE_Reg_outimmediate_7_0), .OutDestReg_2_0(DE_Reg_outdestreg_2_0),
    .OutALU_src(DE_Reg_outalu_src));
  // Probe on DE_Reg_outimmediate_7_0
  Comparator #(.Bits(3)) Match1 (.a(EM_Reg_outdestreg_2_0), .b(Control_readreg2_2_0), .eq(Match1_eq));  // open: gt, lt
  Comparator #(.Bits(3)) Match2 (.a(EM_Reg_outdestreg_2_0), .b(Control_readreg1_2_0), .eq(Match2_eq));  // open: gt, lt
  or or_1 (or_1_out, Match1_eq, Match2_eq);
  Multiplexer #(.Bits(8)) multiplexer_2 (
    .sel(DE_Reg_outalu_src), .in_0(DE_Reg_outregdata2_7_0), .in_1(DE_Reg_outimmediate_7_0), .out(ALU_p2));
  and and_1 (HazardDetected, or_1_out, EM_Reg_outmemread);
  Multiplexer #(.Bits(16)) multiplexer_3 (
    .sel(HazardDetected), .in_0({FD_Reg_outinstr_15_0_2, FD_Reg_outinstr_15_0}), .in_1({16{1'b0}}),
    .out(multiplexer_3_out));
endmodule
