// Digital circuit DE_Register.dig as structural Verilog
module DE_Register (
  input  [7:0] RegData1_7_0,
  input  [7:0] RegData2_7_0,
  input  [4:0] Immediate_4_0,
  input  [7:0] OpCode_7_0,
  input  [2:0] DestReg_2_0,
  input  Clock,
  input  ALU_src,
  output [7:0] OutRegData1_7_0,
  output [7:0] OutRegData2_7_0,
  output [7:0] OutOpCode_7_0,
  output [7:0] OutImmediate_7_0,
  output [2:0] OutDestReg_2_0,
  output OutALU_src
);

  Register #(.Bits(8)) register_1 (.D(RegData1_7_0), .C(Clock), .en(1'b1), .Q(OutRegData1_7_0));
  Register #(.Bits(8)) register_2 (.D(RegData2_7_0), .C(Clock), .en(1'b1), .Q(OutRegData2_7_0));
  Register #(.Bits(5)) register_3 (.D(Immediate_4_0), .C(Clock), .en(1'b1), .Q(OutImmediate_7_0[4:0]));
  Register #(.Bits(8)) register_4 (.D(OpCode_7_0), .C(Clock), .en(1'b1), .Q(OutOpCode_7_0));
  Register #(.Bits(3)) register_5 (.D(DestReg_2_0), .C(Clock), .en(1'b1), .Q(OutDestReg_2_0));
  Register register_6 (.D(ALU_src), .C(Clock), .en(1'b1), .Q(OutALU_src));

  assign OutImmediate_7_0[7:5] = 3'b000;
endmodule
