// Digital circuit EM_Register.dig as structural Verilog
module EM_Register (
  input  [7:0] ALU_Result_7_0,
  input  [2:0] DestReg_2_0,
  input  [2:0] Flags_2_0,
  input  MemWrite,
  input  MemRead,
  input  Clock,
  input  [7:0] OpCode,
  output [7:0] OutALU_Result_7_0,
  output [2:0] OutDestReg_2_0,
  output [2:0] OutFlags_2_0,
  output OutMemWrite,
  output OutMemRead,
  output [7:0] OutOpCode
);

  Register #(.Bits(8)) ALU_Result_Reg (.D(ALU_Result_7_0), .C(Clock), .en(1'b1), .Q(OutALU_Result_7_0));
  Register #(.Bits(3)) DestReg_Reg (.D(DestReg_2_0), .C(Clock), .en(1'b1), .Q(OutDestReg_2_0));
  Register #(.Bits(3)) Flags_Reg (.D(Flags_2_0), .C(Clock), .en(1'b1), .Q(OutFlags_2_0));
  Register MemWrite_Reg (.D(MemWrite), .C(Clock), .en(1'b1), .Q(OutMemWrite));
  Register MemRead_Reg (.D(MemRead), .C(Clock), .en(1'b1), .Q(OutMemRead));
  Register #(.Bits(8)) OpCodeReg (.D(OpCode), .C(Clock), .en(1'b1), .Q(OutOpCode));
endmodule
