// Digital circuit FD_Register.dig as structural Verilog
module FD_Register (
  input  [15:0] Instruction_15_0,
  input  [3:0] PC_3_0,
  input  Clock,
  output [15:0] OutInstr_15_0,
  output [3:0] OutPC_3_0
);

  Register #(.Bits(16)) InstrReg (.D(Instruction_15_0), .C(Clock), .en(1'b1), .Q(OutInstr_15_0));
  Register #(.Bits(4)) PCReg (.D(PC_3_0), .C(Clock), .en(1'b1), .Q(OutPC_3_0));
endmodule
