// Digital circuit MW_Register.dig as structural Verilog
module MW_Register (
  input  Clock,
  input  [7:0] FinalResult_7_0,
  input  [2:0] DestReg_2_0,
  input  WriteEnable,
  input  [2:0] Flags_2_0,
  input  [7:0] OpCode,
  output [7:0] OutResult_7_0,
  output [2:0] OutDestReg_2_0,
  output OutWriteEnable,
  output [2:0] OutFlags_2_0,
  output [7:0] OutOpCode
);

  Register #(.Bits(8)) FinalResult_Reg (.D(FinalResult_7_0), .C(Clock), .en(1'b1), .Q(OutResult_7_0));
  Register #(.Bits(3)) DestReg_Reg (.D(DestReg_2_0), .C(Clock), .en(1'b1), .Q(OutDestReg_2_0));
  Register WriteEnable_Reg (.D(WriteEnable), .C(Clock), .en(1'b1), .Q(OutWriteEnable));
  Register #(.Bits(3)) Flags_Reg (.D(Flags_2_0), .C(Clock), .en(1'b1), .Q(OutFlags_2_0));
  Register #(.Bits(8)) OpCodeReg (.D(OpCode), .C(Clock), .en(1'b1), .Q(OutOpCode));
endmodule
