// Digital circuit adder8bit.dig as structural Verilog
module adder8bit (
  input  [7:0] A,
  input  [7:0] B,
  input  Cin,
  output [7:0] Result_7_0,
  output Cout
);

  wire FA0_carry, FA1_carry, FA2_carry, FA3_carry, FA4_carry, FA5_carry, FA6_carry;

  fullAdder FA0 (.Cin(Cin), .A(A[0]), .B(B[0]), .Carry(FA0_carry), .Sum(Result_7_0[0]));
  fullAdder FA1 (.Cin(FA0_carry), .A(A[1]), .B(B[1]), .Carry(FA1_carry), .Sum(Result_7_0[1]));
  fullAdder FA2 (.Cin(FA1_carry), .A(A[2]), .B(B[2]), .Carry(FA2_carry), .Sum(Result_7_0[2]));
  fullAdder FA3 (.Cin(FA2_carry), .A(A[3]), .B(B[3]), .Carry(FA3_carry), .Sum(Result_7_0[3]));
  fullAdder FA4 (.Cin(FA3_carry), .A(A[4]), .B(B[4]), .Carry(FA4_carry), .Sum(Result_7_0[4]));
  fullAdder FA5 (.Cin(FA4_carry), .A(A[5]), .B(B[5]), .Carry(FA5_carry), .Sum(Result_7_0[5]));
  fullAdder FA6 (.Cin(FA5_carry), .A(A[6]), .B(B[6]), .Carry(FA6_carry), .Sum(Result_7_0[6]));
  fullAdder FA7 (.Cin(FA6_carry), .A(A[7]), .B(B[7]), .Carry(Cout), .Sum(Result_7_0[7]));
endmodule

/* Test case:
A B Cin Result[7:0] Cout
0 0 0 0 0
1 1 0 2 0
1 1 1 3 0
*/
