// Digital circuit alu8bit.dig as structural Verilog
module alu8bit (
  input  [7:0] A_7_0,
  input  [7:0] B_7_0,
  input  [2:0] OpCode_2_0,
  input  FlagWrite,
  input  Clock,
  output Zero_Flag,
  output [7:0] Result_7_0,
  output Carry_Flag
);

  wire nor_1_out;

  adder8bit Adder (.A(A_7_0), .B(B_7_0), .Cin(1'b0), .Result_7_0(Result_7_0), .Cout(Carry_Flag));
  nor nor_1 (nor_1_out, Result_7_0[0], Result_7_0[1], Result_7_0[2], Result_7_0[3], Result_7_0[4], Result_7_0[5], Result_7_0[6], Result_7_0[7]);
  Register register_1 (.D(nor_1_out), .C(Clock), .en(FlagWrite), .Q(Zero_Flag));
endmodule
