// Digital circuit controlUnit.dig as structural Verilog
module controlUnit (
  input  [15:0] Instruction_15_0,
  input  [2:0] Flags_2_0,
  output ALU_src,
  output [7:0] OpCode_7_0,
  output [2:0] ReadReg2_2_0,
  output [2:0] ReadReg1_2_0,
  output WriteEnable,
  output MemRead,
  output MemWrite,
  output [7:0] ALU_OP_7_0,
  output [2:0] WriteReg_2_0,
  output BranchTaken,
  output WriteOutput
);

  wire and_1_out, comparator_2_eq;

  Comparator #(.Bits(8)) comparator_1 (.a(Instruction_15_0[15:8]), .b(8'h29), .eq(WriteOutput));  // open: gt, lt
  Comparator #(.Bits(8)) comparator_2 (.a(Instruction_15_0[15:8]), .b(8'h28), .eq(comparator_2_eq));  // open: gt, lt
  and and_1 (and_1_out, WriteOutput, Flags_2_0[0]);
  ROM #(.AddrBits(8), .Bits(11)) rom_1 (
    .A(Instruction_15_0[15:8]), .sel(1'b1), .D({ALU_OP_7_0, MemWrite, MemRead, WriteEnable}));
  or or_1 (BranchTaken, and_1_out, comparator_2_eq);

  assign ALU_src = ALU_OP_7_0[3];
  assign OpCode_7_0 = Instruction_15_0[15:8];
  assign ReadReg1_2_0 = Instruction_15_0[10:8];
  assign ReadReg2_2_0 = Instruction_15_0[7:5];
  assign WriteReg_2_0 = Instruction_15_0[10:8];

  // Notes on the sheet:
  //   contents of rom_1 (hex, n*v repeats v):
  //   0,9,13,2010,200,1e00,2800,0,0,0,51,59,8*0,a1,a9,0,b9,6*0,f4,0,100
endmodule
