// Digital circuit dataRAM.dig as structural Verilog
module dataRAM (
  input  [7:0] Address_7_0,
  input  [7:0] DataIn_7_0,
  input  MemWrite,
  input  MemRead,
  input  Clock,
  output [7:0] DataOut_7_0
);

  RAMDualPort #(.AddrBits(8), .Bits(8)) ramdualport_1 (
    .A(Address_7_0), .Din(DataIn_7_0), .str(MemWrite), .C(Clock), .ld(MemRead), .D(DataOut_7_0));
endmodule
