// Digital circuit fullAdder.dig as structural Verilog
module fullAdder (
  input  Cin,
  input  A,
  input  B,
  output Carry,
  output Sum
);

  wire halfadder_1_carry, halfadder_2_carry, halfadder_2_sum;

  halfAdder halfadder_1 (.A(Cin), .B(halfadder_2_sum), .Sum(Sum), .Carry(halfadder_1_carry));
  halfAdder halfadder_2 (.A(A), .B(B), .Sum(halfadder_2_sum), .Carry(halfadder_2_carry));
  or or_1 (Carry, halfadder_1_carry, halfadder_2_carry);
endmodule

/* Test case:
A B Cin Carry Sum
0 0 0  0  0
0 0 1  0  1
0 1 0  0  1
0 1 1  1  0
1 0 0  0  1
1 0 1  1  0
1 1 0  1  0
1 1 1  1  1
*/
