// Digital circuit programCounter8.dig as structural Verilog
module programCounter8 (
  input  Clock,
  input  [3:0] LoadData_3_0,
  input  Load,
  input  Clear,
  output [3:0] PC_3_0
);

  CounterPreset #(.Bits(4)) counterpreset_1 (
    .en(1'b1), .C(Clock), .dir(1'b0), .in(LoadData_3_0), .ld(Load), .clr(Clear), .out(PC_3_0));  // open: ovf
endmodule
