// Digital circuit programROM.dig as structural Verilog
module programROM (
  input  [3:0] Address_3_0,
  output [15:0] Instruction_15_0
);

  ROM #(.AddrBits(4), .Bits(16)) rom_1 (.A(Address_3_0), .sel(1'b1), .D(Instruction_15_0));

  // Notes on the sheet:
  //   contents of rom_1 (hex, n*v repeats v):
  //   12f,153,1424,2020,2800
endmodule
