// Digital circuit registerFile8.dig as structural Verilog
module registerFile8 (
  input  [7:0] Din_7_0,
  input  WriteEnable,
  input  [2:0] WriteReg_2_0,
  input  Clock,
  input  [2:0] ReadReg1_2_0,
  input  [2:0] ReadReg2_2_0,
  output [7:0] ReadData1_7_0,
  output [7:0] ReadData2_7_0
);

  RegisterFile #(.AddrBits(3), .Bits(8)) registerfile_1 (
    .Din(Din_7_0), .we(WriteEnable), .Rw(WriteReg_2_0), .C(Clock), .Ra(ReadReg1_2_0), .Rb(ReadReg2_2_0),
    .Da(ReadData1_7_0), .Db(ReadData2_7_0));
endmodule
